// Logisim project single_cycle_CPU.circ as structural Verilog: 9 circuits, main circuit main
module main (
  input  in_1
);

  wire alu_1_zero, clk, control_unit_1_alusrcb, control_unit_1_menwrite, control_unit_1_pcsrc,
       control_unit_1_regwrite;
  wire [1:0] control_unit_1_immsrc, control_unit_1_resultsrc, control_unit_1_ssrc;
  wire [3:0] control_unit_1_alucontrol;
  wire [15:0] addr_processer_1_addr_result;
  wire [31:0] adder_1_out, adder_2_out, alu_1_aluresult, extend_1_immext, multiplexer_1_out,
       multiplexer_2_out, multiplexer_3_out, ram_1_dout, register_1_q, register_file_1_out_8,
       register_file_1_out_9, rom_1_data, s_processer_1_sout;

  Multiplexer #(.width(32)) multiplexer_1 (.in0(adder_1_out), .in1(adder_2_out), .out(multiplexer_1_out));  // open: sel
  Register #(.width(32)) register_1 (.D(multiplexer_1_out), .clk(clk), .Q(register_1_q), .clr(in_1));  // open: en
  ROM #(.addrWidth(16), .dataWidth(32)) rom_1 (.addr({2'b00, register_1_q[15:2]}), .data(rom_1_data));
  Adder #(.width(32)) adder_1 (.a(register_1_q), .b(32'h4), .out(adder_1_out));  // open: cin, cout
  Control_Unit control_unit_1 (
    .Opcode(rom_1_data[6:0]), .funct3(rom_1_data[14:12]), .funct7(rom_1_data[31:25]), .Zero(alu_1_zero),
    .ALUControl(control_unit_1_alucontrol), .ResultSrc(control_unit_1_resultsrc),
    .MenWrite(control_unit_1_menwrite), .ALUSrcB(control_unit_1_alusrcb), .ImmSrc(control_unit_1_immsrc),
    .Regwrite(control_unit_1_regwrite), .Ssrc(control_unit_1_ssrc), .PCSrc(control_unit_1_pcsrc));
  Extend extend_1 (.Instr_3107(rom_1_data[31:7]), .ImmSrc(control_unit_1_immsrc), .ImmExt(extend_1_immext));
  Register_file register_file_1 (
    .in_3(rom_1_data[24:20]), .in_5(rom_1_data[11:7]), .in_1(rom_1_data[19:15]), .in_7(multiplexer_3_out),
    .in_4(in_1), .in_6(control_unit_1_regwrite), .in_2(clk), .out_9(register_file_1_out_9),
    .out_8(register_file_1_out_8));
  Clock clock_1 (.out(clk));
  Multiplexer #(.width(32)) multiplexer_2 (
    .in0(register_file_1_out_9), .in1(extend_1_immext), .out(multiplexer_2_out));  // open: sel
  Adder #(.width(32)) adder_2 (.a(extend_1_immext), .b(register_1_q), .out(adder_2_out));  // open: cin, cout
  ALU alu_1 (
    .SrcB(multiplexer_2_out), .ALUControl(control_unit_1_alucontrol), .SrcA(register_file_1_out_8),
    .Zero(alu_1_zero), .ALUresult(alu_1_aluresult));
  Addr_processer addr_processer_1 (
    .ALUResult(alu_1_aluresult), .Ssrc(control_unit_1_ssrc), .Addr_Result(addr_processer_1_addr_result));
  S_Processer s_processer_1 (.RD2(register_file_1_out_9), .Ssrc(control_unit_1_ssrc), .Sout(s_processer_1_sout));
  RAM #(.addrWidth(16), .asyncread("true"), .dataWidth(32)) ram_1 (
    .addr(addr_processer_1_addr_result), .we(control_unit_1_menwrite), .oe(1'b1), .clk(clk),
    .din(s_processer_1_sout), .dout(ram_1_dout));
  Multiplexer #(.select(2), .width(32)) multiplexer_3 (
    .in0(alu_1_aluresult), .in1(ram_1_dout), .in2(adder_1_out), .out(multiplexer_3_out));  // open: in3, sel

  // Other names for the same wires on the sheet: reset = in_1
endmodule

module Register_file (
  input  [4:0] in_1,
  input  in_2,
  input  [4:0] in_3,
  input  in_4,
  input  [4:0] in_5,
  input  in_6,
  input  [31:0] in_7,
  output [31:0] out_8,
  output [31:0] out_9
);

  wire and_1_out, and_2_out, and_3_out, and_4_out, and_5_out, and_6_out, and_7_out, and_8_out, and_9_out,
       and_10_out, and_11_out, and_12_out, and_13_out, and_14_out, and_15_out, and_16_out, and_17_out,
       and_18_out, and_19_out, and_20_out, and_21_out, and_22_out, and_23_out, and_24_out, and_25_out,
       and_26_out, and_27_out, and_28_out, and_29_out, and_30_out, and_31_out, and_32_out, slt_0, slt_1,
       slt_2, slt_3, slt_4, slt_5, slt_6, slt_7, slt_8, slt_9, slt_10, slt_11, slt_12, slt_13, slt_14,
       slt_15, slt_16, slt_17, slt_18, slt_19, slt_20, slt_21, slt_22, slt_23, slt_24, slt_25, slt_26,
       slt_27, slt_28, slt_29, slt_30, slt_31;
  wire [31:0] multiplexer_3_out, multiplexer_4_out, multiplexer_5_out, multiplexer_6_out, multiplexer_7_out,
       multiplexer_8_out, multiplexer_9_out, multiplexer_10_out, multiplexer_11_out, multiplexer_12_out,
       multiplexer_13_out, multiplexer_14_out, multiplexer_15_out, multiplexer_16_out, multiplexer_17_out,
       multiplexer_18_out, multiplexer_19_out, multiplexer_20_out, multiplexer_21_out, multiplexer_22_out,
       multiplexer_23_out, multiplexer_24_out, multiplexer_25_out, multiplexer_26_out, multiplexer_27_out,
       multiplexer_28_out, multiplexer_29_out, multiplexer_30_out, multiplexer_31_out, multiplexer_32_out,
       multiplexer_33_out, multiplexer_34_out, r0_q, v_1, v_2, v_3, v_4, v_5, v_6, v_7, v_8, v_9, v_10, v_11,
       v_12, v_13, v_14, v_15, v_16, v_17, v_18, v_19, v_20, v_21, v_22, v_23, v_24, v_25, v_26, v_27, v_28,
       v_29, v_30, v_31;

  Decoder #(.select(5)) decoder_1 (
    .out0(slt_0), .out1(slt_1), .out2(slt_2), .out3(slt_3), .out4(slt_4), .out5(slt_5), .out6(slt_6),
    .out7(slt_7), .out8(slt_8), .out9(slt_9), .out10(slt_10), .out11(slt_11), .out12(slt_12), .out13(slt_13),
    .out14(slt_14), .out15(slt_15), .out16(slt_16), .out17(slt_17), .out18(slt_18), .out19(slt_19),
    .out20(slt_20), .out21(slt_21), .out22(slt_22), .out23(slt_23), .out24(slt_24), .out25(slt_25),
    .out26(slt_26), .out27(slt_27), .out28(slt_28), .out29(slt_29), .out30(slt_30), .out31(slt_31),
    .sel(in_5), .en(in_6));
  Multiplexer #(.select(5), .width(32)) multiplexer_1 (
    .in0({32{1'b0}}), .in1(v_1), .in2(v_2), .in3(v_3), .in4(v_4), .in5(v_5), .in6(v_6), .in7(v_7), .in8(v_8),
    .in9(v_9), .in10(v_10), .in11(v_11), .in12(v_12), .in13(v_13), .in14(v_14), .in15(v_15), .in16(v_16),
    .in17(v_17), .in18(v_18), .in19(v_19), .in20(v_20), .in21(v_21), .in22(v_22), .in23(v_23), .in24(v_24),
    .in25(v_25), .in26(v_26), .in27(v_27), .in28(v_28), .in29(v_29), .in30(v_30), .in31(v_31), .out(out_8),
    .sel(in_1));
  Multiplexer #(.select(5), .width(32)) multiplexer_2 (
    .in0({32{1'b0}}), .in1(v_1), .in2(v_2), .in3(v_3), .in4(v_4), .in5(v_5), .in6(v_6), .in7(v_7), .in8(v_8),
    .in9(v_9), .in10(v_10), .in11(v_11), .in12(v_12), .in13(v_13), .in14(v_14), .in15(v_15), .in16(v_16),
    .in17(v_17), .in18(v_18), .in19(v_19), .in20(v_20), .in21(v_21), .in22(v_22), .in23(v_23), .in24(v_24),
    .in25(v_25), .in26(v_26), .in27(v_27), .in28(v_28), .in29(v_29), .in30(v_30), .in31(v_31), .out(out_9),
    .sel(in_3));
  and and_1 (and_1_out, 1'b0, in_6);
  Multiplexer #(.width(32)) multiplexer_3 (.in0({32{1'b0}}), .in1(in_7), .out(multiplexer_3_out), .sel(and_1_out));
  Multiplexer #(.width(32)) multiplexer_4 (.in0(v_1), .in1(in_7), .out(multiplexer_4_out), .sel(and_2_out));
  and and_2 (and_2_out, slt_1, in_6);
  Multiplexer #(.width(32)) multiplexer_5 (.in0(v_2), .in1(in_7), .out(multiplexer_5_out), .sel(and_3_out));
  and and_3 (and_3_out, slt_2, in_6);
  Multiplexer #(.width(32)) multiplexer_6 (.in0(v_3), .in1(in_7), .out(multiplexer_6_out), .sel(and_4_out));
  and and_4 (and_4_out, slt_3, in_6);
  Multiplexer #(.width(32)) multiplexer_7 (.in0(v_4), .in1(in_7), .out(multiplexer_7_out), .sel(and_5_out));
  and and_5 (and_5_out, slt_4, in_6);
  Multiplexer #(.width(32)) multiplexer_8 (.in0(v_5), .in1(in_7), .out(multiplexer_8_out), .sel(and_6_out));
  and and_6 (and_6_out, slt_5, in_6);
  Multiplexer #(.width(32)) multiplexer_9 (.in0(v_6), .in1(in_7), .out(multiplexer_9_out), .sel(and_7_out));
  and and_7 (and_7_out, slt_6, in_6);
  Multiplexer #(.width(32)) multiplexer_10 (.in0(v_7), .in1(in_7), .out(multiplexer_10_out), .sel(and_8_out));
  and and_8 (and_8_out, slt_7, in_6);
  Register #(.width(32)) r0 (.D(multiplexer_3_out), .clk(in_2), .Q(r0_q), .clr(in_4));  // open: en
  Register #(.width(32)) r1 (.D(multiplexer_4_out), .clk(in_2), .Q(v_1), .clr(in_4));  // open: en
  Register #(.width(32)) r2 (.D(multiplexer_5_out), .clk(in_2), .Q(v_2), .clr(in_4));  // open: en
  Register #(.width(32)) r3 (.D(multiplexer_6_out), .clk(in_2), .Q(v_3), .clr(in_4));  // open: en
  Register #(.width(32)) r4 (.D(multiplexer_7_out), .clk(in_2), .Q(v_4), .clr(in_4));  // open: en
  Register #(.width(32)) r5 (.D(multiplexer_8_out), .clk(in_2), .Q(v_5), .clr(in_4));  // open: en
  Register #(.width(32)) r6 (.D(multiplexer_9_out), .clk(in_2), .Q(v_6), .clr(in_4));  // open: en
  Register #(.width(32)) r7 (.D(multiplexer_10_out), .clk(in_2), .Q(v_7), .clr(in_4));  // open: en
  Multiplexer #(.width(32)) multiplexer_11 (.in0(v_8), .in1(in_7), .out(multiplexer_11_out), .sel(and_9_out));
  and and_9 (and_9_out, slt_8, in_6);
  Multiplexer #(.width(32)) multiplexer_12 (.in0(v_9), .in1(in_7), .out(multiplexer_12_out), .sel(and_10_out));
  and and_10 (and_10_out, slt_9, in_6);
  Multiplexer #(.width(32)) multiplexer_13 (.in0(v_10), .in1(in_7), .out(multiplexer_13_out), .sel(and_11_out));
  and and_11 (and_11_out, slt_10, in_6);
  Multiplexer #(.width(32)) multiplexer_14 (.in0(v_11), .in1(in_7), .out(multiplexer_14_out), .sel(and_12_out));
  and and_12 (and_12_out, slt_11, in_6);
  Multiplexer #(.width(32)) multiplexer_15 (.in0(v_12), .in1(in_7), .out(multiplexer_15_out), .sel(and_13_out));
  and and_13 (and_13_out, slt_12, in_6);
  Multiplexer #(.width(32)) multiplexer_16 (.in0(v_13), .in1(in_7), .out(multiplexer_16_out), .sel(and_14_out));
  and and_14 (and_14_out, slt_13, in_6);
  Multiplexer #(.width(32)) multiplexer_17 (.in0(v_14), .in1(in_7), .out(multiplexer_17_out), .sel(and_15_out));
  and and_15 (and_15_out, slt_14, in_6);
  Multiplexer #(.width(32)) multiplexer_18 (.in0(v_15), .in1(in_7), .out(multiplexer_18_out), .sel(and_16_out));
  and and_16 (and_16_out, slt_15, in_6);
  Register #(.width(32)) r8 (.D(multiplexer_11_out), .clk(in_2), .Q(v_8), .clr(in_4));  // open: en
  Register #(.width(32)) r9 (.D(multiplexer_12_out), .clk(in_2), .Q(v_9), .clr(in_4));  // open: en
  Register #(.width(32)) r10 (.D(multiplexer_13_out), .clk(in_2), .Q(v_10), .clr(in_4));  // open: en
  Register #(.width(32)) r11 (.D(multiplexer_14_out), .clk(in_2), .Q(v_11), .clr(in_4));  // open: en
  Register #(.width(32)) r12 (.D(multiplexer_15_out), .clk(in_2), .Q(v_12), .clr(in_4));  // open: en
  Register #(.width(32)) r13 (.D(multiplexer_16_out), .clk(in_2), .Q(v_13), .clr(in_4));  // open: en
  Register #(.width(32)) r14 (.D(multiplexer_17_out), .clk(in_2), .Q(v_14), .clr(in_4));  // open: en
  Register #(.width(32)) r15 (.D(multiplexer_18_out), .clk(in_2), .Q(v_15), .clr(in_4));  // open: en
  Multiplexer #(.width(32)) multiplexer_19 (.in0(v_16), .in1(in_7), .out(multiplexer_19_out), .sel(and_17_out));
  and and_17 (and_17_out, slt_16, in_6);
  Multiplexer #(.width(32)) multiplexer_20 (.in0(v_17), .in1(in_7), .out(multiplexer_20_out), .sel(and_18_out));
  and and_18 (and_18_out, slt_17, in_6);
  Multiplexer #(.width(32)) multiplexer_21 (.in0(v_18), .in1(in_7), .out(multiplexer_21_out), .sel(and_19_out));
  and and_19 (and_19_out, slt_18, in_6);
  Multiplexer #(.width(32)) multiplexer_22 (.in0(v_19), .in1(in_7), .out(multiplexer_22_out), .sel(and_20_out));
  and and_20 (and_20_out, slt_19, in_6);
  Multiplexer #(.width(32)) multiplexer_23 (.in0(v_20), .in1(in_7), .out(multiplexer_23_out), .sel(and_21_out));
  and and_21 (and_21_out, slt_20, in_6);
  Multiplexer #(.width(32)) multiplexer_24 (.in0(v_21), .in1(in_7), .out(multiplexer_24_out), .sel(and_22_out));
  and and_22 (and_22_out, slt_21, in_6);
  Multiplexer #(.width(32)) multiplexer_25 (.in0(v_22), .in1(in_7), .out(multiplexer_25_out), .sel(and_23_out));
  and and_23 (and_23_out, slt_22, in_6);
  Multiplexer #(.width(32)) multiplexer_26 (.in0(v_23), .in1(in_7), .out(multiplexer_26_out), .sel(and_24_out));
  and and_24 (and_24_out, slt_23, in_6);
  Register #(.width(32)) r16 (.D(multiplexer_19_out), .clk(in_2), .Q(v_16), .clr(in_4));  // open: en
  Register #(.width(32)) r17 (.D(multiplexer_20_out), .clk(in_2), .Q(v_17), .clr(in_4));  // open: en
  Register #(.width(32)) r18 (.D(multiplexer_21_out), .clk(in_2), .Q(v_18), .clr(in_4));  // open: en
  Register #(.width(32)) r19 (.D(multiplexer_22_out), .clk(in_2), .Q(v_19), .clr(in_4));  // open: en
  Register #(.width(32)) r20 (.D(multiplexer_23_out), .clk(in_2), .Q(v_20), .clr(in_4));  // open: en
  Register #(.width(32)) r21 (.D(multiplexer_24_out), .clk(in_2), .Q(v_21), .clr(in_4));  // open: en
  Register #(.width(32)) r22 (.D(multiplexer_25_out), .clk(in_2), .Q(v_22), .clr(in_4));  // open: en
  Register #(.width(32)) r23 (.D(multiplexer_26_out), .clk(in_2), .Q(v_23), .clr(in_4));  // open: en
  Multiplexer #(.width(32)) multiplexer_27 (.in0(v_24), .in1(in_7), .out(multiplexer_27_out), .sel(and_25_out));
  and and_25 (and_25_out, slt_24, in_6);
  Multiplexer #(.width(32)) multiplexer_28 (.in0(v_25), .in1(in_7), .out(multiplexer_28_out), .sel(and_26_out));
  and and_26 (and_26_out, slt_25, in_6);
  Multiplexer #(.width(32)) multiplexer_29 (.in0(v_26), .in1(in_7), .out(multiplexer_29_out), .sel(and_27_out));
  and and_27 (and_27_out, slt_26, in_6);
  Multiplexer #(.width(32)) multiplexer_30 (.in0(v_27), .in1(in_7), .out(multiplexer_30_out), .sel(and_28_out));
  and and_28 (and_28_out, slt_27, in_6);
  Multiplexer #(.width(32)) multiplexer_31 (.in0(v_28), .in1(in_7), .out(multiplexer_31_out), .sel(and_29_out));
  and and_29 (and_29_out, slt_28, in_6);
  Multiplexer #(.width(32)) multiplexer_32 (.in0(v_29), .in1(in_7), .out(multiplexer_32_out), .sel(and_30_out));
  and and_30 (and_30_out, slt_29, in_6);
  Multiplexer #(.width(32)) multiplexer_33 (.in0(v_30), .in1(in_7), .out(multiplexer_33_out), .sel(and_31_out));
  and and_31 (and_31_out, slt_30, in_6);
  Multiplexer #(.width(32)) multiplexer_34 (.in0(v_31), .in1(in_7), .out(multiplexer_34_out), .sel(and_32_out));
  and and_32 (and_32_out, slt_31, in_6);
  Register #(.width(32)) r24 (.D(multiplexer_27_out), .clk(in_2), .Q(v_24), .clr(in_4));  // open: en
  Register #(.width(32)) r25 (.D(multiplexer_28_out), .clk(in_2), .Q(v_25), .clr(in_4));  // open: en
  Register #(.width(32)) r26 (.D(multiplexer_29_out), .clk(in_2), .Q(v_26), .clr(in_4));  // open: en
  Register #(.width(32)) r27 (.D(multiplexer_30_out), .clk(in_2), .Q(v_27), .clr(in_4));  // open: en
  Register #(.width(32)) r28 (.D(multiplexer_31_out), .clk(in_2), .Q(v_28), .clr(in_4));  // open: en
  Register #(.width(32)) r29 (.D(multiplexer_32_out), .clk(in_2), .Q(v_29), .clr(in_4));  // open: en
  Register #(.width(32)) r30 (.D(multiplexer_33_out), .clk(in_2), .Q(v_30), .clr(in_4));  // open: en
  Register #(.width(32)) r31 (.D(multiplexer_34_out), .clk(in_2), .Q(v_31), .clr(in_4));  // open: en
  // also tied to GND on the sheet: {r0_q[0], r0_q[1], r0_q[2], r0_q[3], r0_q[4], r0_q[5], r0_q[6], r0_q[7], r0_q[8], r0_q[9], r0_q[10], r0_q[11], r0_q[12], r0_q[13], r0_q[14], r0_q[15], r0_q[16], r0_q[17], r0_q[18], r0_q[19], r0_q[20], r0_q[21], r0_q[22], r0_q[23], r0_q[24], r0_q[25], r0_q[26], r0_q[27], r0_q[28], r0_q[29], r0_q[30], r0_q[31]}

  // Other names for the same wires on the sheet: A1[4:0] = in_1; A2[4:0] = in_3; A3[4:0] = in_5; clk = in_2;
  //   RD1[31:0] = out_8; RD2[31:0] = out_9; reset = in_4; WD[31:0] = in_7; WE = in_6
endmodule

module ALU (
  input  [31:0] SrcA,
  input  [31:0] SrcB,
  input  [3:0] ALUControl,
  output Zero,
  output [31:0] ALUresult
);

  wire comparator_1_lt, comparator_2_lt;
  wire [31:0] adder_1_out, and_1_out, bit_extender_1_out, bit_extender_2_out, or_1_out, shifter_1_out,
       shifter_2_out, shifter_3_out, subtractor_1_out, xor_1_out;

  Adder #(.width(32)) adder_1 (.a(SrcA), .b(SrcB), .out(adder_1_out));  // open: cin, cout
  Subtractor #(.width(32)) subtractor_1 (.a(SrcA), .b(SrcB), .out(subtractor_1_out));  // open: bin, bout
  Comparator #(.width(32)) comparator_1 (.a(SrcA), .b(SrcB), .lt(comparator_1_lt));  // open: gt, eq
  Shifter #(.width(32)) shifter_1 (.in(SrcA), .\dist (SrcB[4:0]), .out(shifter_1_out));
  Shifter #(.shift("lr"), .width(32)) shifter_2 (.in(SrcA), .\dist (SrcB[4:0]), .out(shifter_2_out));
  Shifter #(.shift("ar"), .width(32)) shifter_3 (.in(SrcA), .\dist (SrcB[4:0]), .out(shifter_3_out));
  Comparator #(.mode("unsigned"), .width(32)) comparator_2 (.a(SrcA), .b(SrcB), .lt(comparator_2_lt));  // open: gt, eq
  assign and_1_out = SrcA & SrcB;  // AND_Gate and_1, 32 bits wide
  assign or_1_out = SrcA | SrcB;  // OR_Gate or_1, 32 bits wide
  assign xor_1_out = SrcA ^ SrcB;  // XOR_Gate xor_1, 32 bits wide
  assign bit_extender_1_out = {{31{1'b0}}, comparator_1_lt};  // Bit_Extender bit_extender_1
  assign bit_extender_2_out = {{31{1'b0}}, comparator_2_lt};  // Bit_Extender bit_extender_2
  Comparator #(.width(32)) comparator_3 (.a({32{1'b0}}), .b(subtractor_1_out), .eq(Zero));  // open: gt, lt
  Multiplexer #(.select(4), .width(32)) multiplexer_1 (
    .in0(adder_1_out), .in1(subtractor_1_out), .in2(and_1_out), .in3(or_1_out), .in4(bit_extender_1_out),
    .in5(shifter_1_out), .in6(shifter_2_out), .in7(shifter_3_out), .in8(xor_1_out), .in9(bit_extender_2_out),
    .out(ALUresult), .sel(ALUControl));  // open: in10, in11, in12, in13, in14, in15
endmodule

module Extend (
  input  [24:0] Instr_3107,
  input  [1:0] ImmSrc,
  output [31:0] ImmExt
);

  wire [11:0] bit_extender_4_out;
  wire [19:0] bit_extender_3_out;
  wire [20:0] bit_extender_1_out, bit_extender_2_out;

  assign bit_extender_1_out = {{20{Instr_3107[24]}}, Instr_3107[24]};  // Bit_Extender bit_extender_1
  assign bit_extender_2_out = {{20{Instr_3107[24]}}, Instr_3107[24]};  // Bit_Extender bit_extender_2
  assign bit_extender_3_out = {{19{Instr_3107[24]}}, Instr_3107[24]};  // Bit_Extender bit_extender_3
  assign bit_extender_4_out = {{11{Instr_3107[24]}}, Instr_3107[24]};  // Bit_Extender bit_extender_4
  Multiplexer #(.select(2), .width(32)) multiplexer_1 (
    .in0({bit_extender_1_out, Instr_3107[23:13]}),
    .in1({bit_extender_2_out, Instr_3107[23:18], Instr_3107[4:0]}),
    .in2({bit_extender_3_out, Instr_3107[0], Instr_3107[23:18], Instr_3107[4:1], 1'b0}),
    .in3({bit_extender_4_out, Instr_3107[12:5], Instr_3107[13], Instr_3107[23:14], 1'b0}), .out(ImmExt),
    .sel(ImmSrc));

  // Notes on the sheet:
  //   I1
  //   S
  //   B
  //   J
endmodule

module Main_Decoder (
  input  [2:0] funct3,
  input  [6:0] Opcode,
  output RegWrite,
  output Branch,
  output Jump,
  output ALUSrcB,
  output [1:0] ALUOp,
  output [1:0] Ssrc,
  output MenWrite,
  output [1:0] ResultSrc,
  output [1:0] ImmSrc
);

  wire I1_Imm, not_1_out, not_2_out, not_3_out, not_4_out, not_5_out, not_6_out, not_7_out, not_8_out,
       not_9_out, R, sb;

  not not_1 (not_1_out, Opcode[1]);
  not not_2 (not_2_out, Opcode[0]);
  not not_3 (not_3_out, Opcode[2]);
  not not_4 (not_4_out, Opcode[3]);
  not not_5 (not_5_out, Opcode[4]);
  not not_6 (not_6_out, Opcode[5]);
  not not_7 (not_7_out, Opcode[6]);
  not not_8 (not_8_out, funct3[0]);
  not not_9 (not_9_out, funct3[1]);
  and and_1 (ResultSrc[0], Opcode[0], Opcode[1], not_3_out, not_4_out, not_5_out, not_6_out, not_7_out);
  and and_2 (Ssrc[1], not_8_out, Opcode[0], Opcode[1], not_3_out, not_4_out, not_5_out, Opcode[5], not_7_out, funct3[1]);
  and and_3 (R, Opcode[0], Opcode[1], not_3_out, not_4_out, Opcode[4], Opcode[5], not_7_out);
  and and_4 (ALUOp[0], Opcode[0], Opcode[1], not_3_out, not_4_out, not_5_out, Opcode[5], Opcode[6]);
  and and_5 (sb, Opcode[0], Opcode[1], not_3_out, not_4_out, not_5_out, Opcode[5], not_7_out, not_8_out, not_9_out);
  and and_6 (Ssrc[0], Opcode[0], Opcode[1], not_3_out, not_4_out, not_5_out, Opcode[5], not_7_out, funct3[0], not_9_out);
  and and_7 (I1_Imm, Opcode[0], Opcode[1], not_3_out, not_4_out, Opcode[4], not_6_out, not_7_out);
  and and_8 (Jump, Opcode[0], Opcode[1], Opcode[2], Opcode[3], not_5_out, Opcode[5], Opcode[6]);
  or or_1 (RegWrite, ResultSrc[0], R, I1_Imm, Jump);
  or or_2 (ImmSrc[0], MenWrite, Jump);
  or or_3 (ImmSrc[1], ALUOp[0], Jump);
  or or_4 (MenWrite, Ssrc[1], sb, Ssrc[0]);
  or or_5 (ALUSrcB, ResultSrc[0], MenWrite, I1_Imm);
  or or_6 (ALUOp[1], R, I1_Imm);

  assign Branch = ALUOp[0];
  assign ResultSrc[1] = Jump;

  // Other names for the same wires on the sheet: ALUOp_0 = ALUOp[0]; B_Branch = ALUOp[0]; ALUOp_1 = ALUOp[1];
  //   funct3_0 = funct3[0]; funct3_1 = funct3[1]; funct3_2 = funct3[2]; ImmSrc_0 = ImmSrc[0]; ImmSrc_1 = ImmSrc[1];
  //   op0 = Opcode[0]; op1 = Opcode[1]; op2 = Opcode[2]; op3 = Opcode[3]; op4 = Opcode[4]; op5 = Opcode[5];
  //   op6 = Opcode[6]; I1_Load = ResultSrc[0]; ResultSrc_0 = ResultSrc[0]; J = Jump; ResultSrc_1 = Jump;
  //   S_Store = MenWrite; sh = Ssrc[0]; Ssrc_0 = Ssrc[0]; Ssrc_1 = Ssrc[1]; sw = Ssrc[1]
endmodule

module ALU_Decoder (
  input  [6:0] funct7,
  input  Opcode_5,
  input  [2:0] funct3,
  input  [1:0] ALUOp,
  output [3:0] ALUControl
);

  wire a_nd, add, addi, and_1_out, and_2_out, and_4_out, and_6_out, and_7_out, and_8_out, and_12_out,
       and_13_out, andi, bne, lw, nand_1_out, not_1_out, not_2_out, not_3_out, not_4_out, not_5_out,
       not_6_out, not_7_out, not_8_out, not_9_out, not_10_out, not_11_out, not_12_out, not_13_out,
       not_14_out, o_r, ori, sllr, slt, slti, sltu, sltui, srav, srlr, sub, sw, xori, xorr;

  not not_1 (not_1_out, ALUOp[1]);
  not not_2 (not_2_out, ALUOp[0]);
  not not_3 (not_3_out, funct3[0]);
  or or_1 (ALUControl[0], ori, o_r, srav, sltui, sllr, sub, sltu);
  not not_4 (not_4_out, funct3[1]);
  not not_5 (not_5_out, funct3[2]);
  not not_6 (not_6_out, Opcode_5);
  not not_7 (not_7_out, funct7[5]);
  and and_1 (and_1_out, Opcode_5, funct7[5]);
  or or_2 (ALUControl[1], a_nd, andi, bne, o_r, ori, srlr, srav);
  nand nand_1 (nand_1_out, Opcode_5, funct7[5]);
  and and_2 (and_2_out, not_1_out, not_2_out);
  and and_3 (bne, not_1_out, ALUOp[0]);
  and and_4 (and_4_out, ALUOp[1], not_2_out, not_3_out, not_4_out, not_5_out, nand_1_out);
  and and_5 (sub, ALUOp[1], not_2_out, not_3_out, not_4_out, not_5_out, and_1_out);
  and and_6 (and_6_out, ALUOp[1], not_2_out, not_3_out, funct3[1], not_5_out);
  and and_7 (and_7_out, ALUOp[1], not_2_out, not_3_out, funct3[1], funct3[2]);
  and and_8 (and_8_out, ALUOp[1], not_2_out, funct3[0], funct3[1], funct3[2]);
  and and_9 (sllr, ALUOp[1], not_2_out, funct3[0], not_4_out, not_5_out, Opcode_5, not_7_out);
  and and_10 (srlr, ALUOp[1], not_2_out, funct3[0], not_4_out, funct3[2], Opcode_5, not_7_out);
  and and_11 (srav, ALUOp[1], not_2_out, funct3[0], not_4_out, funct3[2], Opcode_5, funct7[5]);
  and and_12 (and_12_out, ALUOp[1], not_2_out, not_3_out, not_4_out, funct3[2], Opcode_5, not_7_out);
  and and_13 (and_13_out, ALUOp[1], not_2_out, funct3[0], funct3[1], not_5_out, Opcode_5, not_7_out);
  assign {sw, lw} = {{1{and_2_out}}, and_2_out};  // Bit_Extender bit_extender_1
  assign {addi, add} = {{1{and_4_out}}, and_4_out};  // Bit_Extender bit_extender_2
  assign {slti, slt} = {{1{and_6_out}}, and_6_out};  // Bit_Extender bit_extender_3
  assign {ori, o_r} = {{1{and_7_out}}, and_7_out};  // Bit_Extender bit_extender_4
  assign {andi, a_nd} = {{1{and_8_out}}, and_8_out};  // Bit_Extender bit_extender_5
  assign {xorr, xori} = {{1{and_12_out}}, and_12_out};  // Bit_Extender bit_extender_6
  assign {sltu, sltui} = {{1{and_13_out}}, and_13_out};  // Bit_Extender bit_extender_7
  not not_8 (not_8_out, ALUOp[1]);
  or or_3 (ALUControl[2], slt, sllr, slti, srav, srlr);
  not not_9 (not_9_out, ALUOp[0]);
  not not_10 (not_10_out, funct3[0]);
  not not_11 (not_11_out, funct3[1]);
  not not_12 (not_12_out, funct3[2]);
  not not_13 (not_13_out, Opcode_5);
  or or_4 (ALUControl[3], xorr, xori, sltui, sltu);
  not not_14 (not_14_out, funct7[5]);

  // Other names for the same wires on the sheet: ALUControl_0 = ALUControl[0]; ALUControl_1 = ALUControl[1];
  //   ALUControl_2 = ALUControl[2]; ALUControl_3 = ALUControl[3]; ALUOp_01[1:0] = ALUOp; funct3_0 = funct3[0];
  //   funct3_1 = funct3[1]; funct3_2 = funct3[2]; funct7_5 = funct7[5]; Op_5 = Opcode_5
endmodule

module Control_Unit (
  input  Zero,
  input  [6:0] Opcode,
  input  [2:0] funct3,
  input  [6:0] funct7,
  output PCSrc,
  output [1:0] ResultSrc,
  output MenWrite,
  output ALUSrcB,
  output [1:0] ImmSrc,
  output Regwrite,
  output [1:0] Ssrc,
  output [3:0] ALUControl
);

  wire and_1_out, main_decoder_1_branch, main_decoder_1_jump, not_1_out;
  wire [1:0] main_decoder_1_aluop;

  Main_Decoder main_decoder_1 (
    .Opcode(Opcode), .MenWrite(MenWrite), .ALUOp(main_decoder_1_aluop), .RegWrite(Regwrite),
    .ALUSrcB(ALUSrcB), .Ssrc(Ssrc), .Branch(main_decoder_1_branch), .Jump(main_decoder_1_jump),
    .ImmSrc(ImmSrc), .ResultSrc(ResultSrc));  // open: funct3
  ALU_Decoder alu_decoder_1 (
    .funct3(funct3), .ALUOp(main_decoder_1_aluop), .funct7(funct7), .Opcode_5(Opcode[5]),
    .ALUControl(ALUControl));
  not not_1 (not_1_out, Zero);
  and and_1 (and_1_out, not_1_out, main_decoder_1_branch);
  or or_1 (PCSrc, and_1_out, main_decoder_1_jump);
endmodule

module S_Processer (
  input  [31:0] RD2,
  input  [1:0] Ssrc,
  output [31:0] Sout
);

  wire [31:0] bit_extender_1_out, bit_extender_2_out;

  assign bit_extender_1_out = {{24{RD2[7]}}, RD2[7:0]};  // Bit_Extender bit_extender_1
  assign bit_extender_2_out = {{16{RD2[15]}}, RD2[15:0]};  // Bit_Extender bit_extender_2
  Multiplexer #(.select(2), .width(32)) multiplexer_1 (
    .in0(bit_extender_1_out), .in1(bit_extender_2_out), .in2(RD2), .out(Sout), .sel(Ssrc));  // open: in3
endmodule

module Addr_processer (
  input  [31:0] ALUResult,
  input  [1:0] Ssrc,
  output [15:0] Addr_Result
);

  wire [15:0] bit_extender_1_out;

  assign bit_extender_1_out = {{8{ALUResult[7]}}, ALUResult[7:0]};  // Bit_Extender bit_extender_1
  Multiplexer #(.select(2), .width(16)) multiplexer_1 (
    .in0(bit_extender_1_out), .in1(ALUResult[15:0]), .in2(ALUResult[15:0]), .out(Addr_Result), .sel(Ssrc));  // open: in3
endmodule
